# Fritzing sketch Schematics (saved by Fritzing 1.0.6)

parts:
  Part1 = 4x Matrix LED 8x8 with MAX7219 [part_number=FC-16]
  A1 = Esp32-c3 super mini
  M1 = BME280
  BAT1 = Battery Holders [package=lipo-1100mAh]
  MOD1 = MT3608 Boost No usb
  U1 = SWITCH_SPDT [package=kps-1290]
  A2 = DWEII Type-C USB 5V 2A Boost Converter Module
  Sensor1 = TTP223B Capacitive Touch Sensor Module
  J1 = Piezo Speaker

nets:
  VCC: Part1.VCC, M1.VIN, Sensor1.VCC
  GND: Part1.GND, M1.GND
  N1: Part1.CS, A1.Pin_2
  N2: Part1.CLK, A1.Pin_3
  N3: Part1.DIN, A1.Pin_1
  N4: A1.Pin_4, M1.SCL
  N5: A1.Pin_5, M1.SDA
  N6: A1.Pin_6, Sensor1.SIG
  N7: A1.Pin_12, J1.pin2
  N8: A1.Pin_15, BAT1.-, MOD1.IN_(-), MOD1.OUT_(-), A2.BAT-
  N9: A1.Pin_16, U1.O
  N10: BAT1.+, MOD1.IN_(+), A2.BAT+
  N11: MOD1.OUT_(+), U1.P
  N12: Sensor1.GND, J1.pin1

custom parts:
  4x Matrix LED 8x8 with MAX7219: FC-16
  Esp32-c3 super mini: ESP32-C3 Development Board ESP32 SuperMini Development Board ESP32 Development Board WiFi Bluetooth.
  BME280: Temperature Humidity Barometric presure Sensor
  MT3608 Boost No usb: Chip- MT3608 / B6289 DC to DC step up, power booster module. With adjustable output voltage. Current- 2A . || Input voltage- 2V-24V || Output voltage- 5V-28V Input interface- Inversed polarity- NO. || Led indicator- No.
  TTP223B Capacitive Touch Sensor Module: The TTP223B capacitive touch sensor module uses the TTP223B IC. The appropriate voltage is approximately 2 to 5.5 volts.
